# Fritzing sketch Relay (saved by Fritzing 0.7.11b)
breadboards: 1

parts:
  K1 = Relay [part_number=FRS1B-S package=THT]
  Q2 = NPN-Transistor [package="TO92 [THT]"]
  D2 = Rectifier Diode [part_number=1N4001 package="300 mil [THT]"]
  RaspberryPi = Raspberry Pi Model B
  1K = 1k Ω Resistor [package=THT]
  LED1 = LED - 3mm [color="Red (633nm)" package="3 mm [THT]"]
  220 = 220 Ω Resistor [package=THT]

nets:
  N1: K1.COIL1, Q2.C, D2.anode
  N2: K1.C1, K1.C2, K1.COIL2, D2.cathode, RaspberryPi.5V
  N3: K1.B, 220.Pin_1
  N4: Q2.E, RaspberryPi.GND, LED1.cathode
  N5: Q2.B, 1K.Pin_0
  N6: RaspberryPi.#4, 1K.Pin_1
  N7: LED1.anode, 220.Pin_0

custom parts:
  Raspberry Pi Model B: Raspberry Pi (Model B)
